# Fritzing sketch 3_sonar (saved by Fritzing 0.8.7b)
breadboards: 1

parts:
  Part2 = SRF05 Ultrasonic Rangefinder
  Part4 = Arduino Uno (Rev3)

nets:
  VCC: Part2.VCC, Part4.5V
  N1: Part2.Trig, Part4.D12/MISO
  N2: Part2.Echo, Part4.D11_PWM/MOSI
  GND: Part2.GND, Part4.GND
