# Fritzing sketch 4_meteo_dht (saved by Fritzing 0.8.7b)
breadboards: 1

parts:
  DHT1 = DHT11 Humitidy and Temperature Sensor
  Part4 = Arduino Uno (Rev3)

nets:
  VDD: DHT1.VDD, Part4.5V
  N1: DHT1.DATA, Part4.D7
  GND: DHT1.GND, Part4.GND

custom parts:
  DHT11 Humitidy and Temperature Sensor: DHT11 Humidity and Temperature Sensor
